# Fritzing sketch car_buddy_fritzing (saved by Fritzing 0.9.5d)
breadboards: 4

parts:
  esp1 = ESP32 DevKitc V4
  DS1 = DS18B20 1-Wire Temperature Sensor [part_number=DS18B20]
  LCD1 = 2.8" SPI TFT Module [part_number=MSP2807]
  SP1 = SPEAKER [package=pcb_mount_speaker]
  パーツ1 = InvenSense MPU6050
  M1 = PAM8403 Stereo Amplifier [part_number=HW-104]
  R1 = Resistor [tolerance=±5% resistance=220 package="1206 [SMD]"]
  R2 = Resistor [tolerance=±5% resistance=220 package="1206 [SMD]"]
  R3 = Resistor [tolerance=±5% resistance=220 package="1206 [SMD]"]
  RE1 = Rotary Encoder [package=THT]

nets:
  N1: esp1.IO15, LCD1.pin3
  N2: esp1.IO2, LCD1.pin5
  N3: esp1.IO4, LCD1.pin4
  N4: esp1.IO16, パーツ1.SDA, R3.Pin_1
  N5: esp1.IO17, パーツ1.SCL, R2.Pin_1
  N6: esp1.IO5, LCD1.pin18, RE1.EncoderPinA
  N7: esp1.IO18, LCD1.pin7, LCD1.pin15
  N8: esp1.IO19, LCD1.pin16
  N9: esp1.IO23, LCD1.pin6, LCD1.pin17
  3V3: esp1.3V3, DS1.VDD, LCD1.pin1, LCD1.pin8, パーツ1.VCC, R1.Pin_0, R2.Pin_0, R3.Pin_0
  N10: esp1.IO25, DS1.DQ, M1.INPUTL, R1.Pin_1
  N11: esp1.IO26, M1.INPUTR
  N12: esp1.IO12, RE1.EncoderPinB
  GND: esp1.GND#32, DS1.GND, LCD1.pin2, パーツ1.GND, パーツ1.AD0, M1.POWER-, M1.INPUTG, RE1.EncoderPinC
  N13: esp1.5V, M1.POWER+
  N14: SP1.+, M1.LOUT-
  N15: SP1.-, M1.LOUT+

custom parts:
  ESP32 DevKitc V4: ESP32-DevKitC board with ESP32-WROOM-32 module. ESP32-DevKitC V4 is a small-sized ESP32-based development board produced by Espressif. Most of the pins on the ESP module are broken out to the pin headers on the board. The pins D0, D1, D2, D3, CMD and CLK are used internally for communication between ESP32 and SPI flash memory. They are grouped on both sides near the USB connector. Avoid using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
  2.8" SPI TFT Module: A generic 2.8 inch LCD TFT 320x240 display with touchscreen and SD card slot. Uses the ILI9341 controller, like the Adafruit displays of this size uses.
  PAM8403 Stereo Amplifier: PAM8403 stereo amplifier module Descriptive words Links: PAM8403 product datasheet
